# Fritzing sketch 2-single-led (saved by Fritzing 0.9.3b)
breadboards: 1

parts:
  Part1 = Arduino Uno (Rev3)
  LED1 = LED - 5mm [color="Red (633nm)" package="5 mm [THT]"]

nets:
  N1: Part1.D11_PWM/MOSI, LED1.anode
  N2: Part1.GND, LED1.cathode
